# Fritzing sketch sketch_P1 (saved by Fritzing 0.9.10b)
breadboards: 1

parts:
  R1 = Resistor [tolerance=±5% resistance=10k package="1206 [SMD]"]
  S1 = Pushbutton [package="[THT]"]
  Part1 = Arduino Uno (Rev3)
  LED1 = LED - 5mm [color="Green (555nm)" current=0.030 package="5 mm [THT]"]
  R2 = Resistor [tolerance=±5% power=0.25 resistance=220 package=THT]

nets:
  N1: R1.Pin_0, Part1.D2
  N2: R1.Pin_1, S1.Pin_1, S1.Pin_2, Part1.GND, LED1.cathode
  N3: S1.Pin_3, S1.Pin_4, Part1.5V
  N4: Part1.D9_PWM, R2.Pin_0
  N5: LED1.anode, R2.Pin_1
