# Fritzing sketch sketch_P3 (saved by Fritzing 0.9.10b)
breadboards: 1

parts:
  Part1 = Arduino Uno (Rev3)
  LED1 = LED - 5mm [color="Green (555nm)" current=0.030 package="5 mm [THT]"]
  R2 = Resistor [tolerance=±5% power=0.25 resistance=220 package=THT]

nets:
  N1: Part1.D9_PWM, R2.Pin_0
  N2: Part1.GND, LED1.cathode
  N3: LED1.anode, R2.Pin_1
