# Fritzing sketch sketch_P1 (saved by Fritzing 0.9.10b)
breadboards: 1

parts:
  Part1 = Arduino Uno (Rev3)
  LED1 = smd LED [color="Yellow (595nm)" package="0603 [SMD]"]
  R2 = Resistor [tolerance=±5% resistance=220 package="2010 [SMD]"]

nets:
  N1: Part1.D10_PWM/SS, R2.Pin_1
  N2: Part1.GND, LED1.cathode
  N3: LED1.anode, R2.Pin_0
