# Fritzing sketch sketch_P3 (saved by Fritzing 0.9.10b)
breadboards: 1

parts:
  Part1 = Arduino Uno (Rev3)
  R1 = PHOTOCELL [package=photocell-kit]
  R2 = Rotary Potentiometer (Small) [maximum_resistance=100kΩ knob_status=50% power=0.5W package=THT]
  R3 = Resistor [tolerance=±5% resistance=220 package="0805 [SMD]"]

nets:
  N1: Part1.A0, R2.wiper
  N2: Part1.A1, R1.P$1, R3.Pin_1
  N3: Part1.5V, R3.Pin_0
  N4: Part1.GND, R1.P$2, R2.leg1, R2.leg2
