# Fritzing sketch sketch_P1 (saved by Fritzing 0.9.10b)
breadboards: 1

parts:
  Part1 = Arduino Uno (Rev3)
  R1 = Resistor [tolerance=±5% power=0.25 resistance=220 package=THT]
  LED1 = LED - 3mm [color="Yellow (595nm)" current=0.030 package="3 mm [THT]"]
  LED2 = LED - 3mm [color="Red (633nm)" current=0.030 package="3 mm [THT]"]
  R2 = Resistor [tolerance=±5% power=0.25 resistance=220 package=THT]

nets:
  N1: Part1.D9_PWM, R2.Pin_1
  N2: Part1.D11_PWM/MOSI, R1.Pin_1
  N3: Part1.GND, LED1.cathode, LED2.cathode
  N4: R1.Pin_0, LED1.anode
  N5: LED2.anode, R2.Pin_0
