# Fritzing sketch sketch_P3 (saved by Fritzing 0.9.10b)
breadboards: 1

parts:
  Part1 = Arduino Uno (Rev3)
  LCD1 = LCD screen
  R1 = Resistor [tolerance=±5% resistance=220 package="1206 [SMD]"]
  R2 = Rotary Potentiometer (Small) [maximum_resistance=100kΩ knob_status=50% power=0.5W package=THT]

nets:
  N1: Part1.A0, LCD1.V0, R2.wiper
  N2: Part1.D11_PWM/MOSI, LCD1.E
  N3: Part1.D12/MISO, LCD1.RS
  GND: Part1.GND, LCD1.VSS, LCD1.R/W, LCD1.LED-
  N4: Part1.D2, LCD1.DB4
  N5: Part1.D3_PWM, LCD1.DB5
  N6: Part1.D4, LCD1.DB6
  N7: Part1.D5_PWM, LCD1.DB7
  5V: Part1.5V, LCD1.VDD, R1.Pin_1
  N8: LCD1.LED+, R1.Pin_0
