# Fritzing sketch sketch (saved by Fritzing 0.9.10b)
breadboards: 1

parts:
  Part1 = Arduino Uno (Rev3)
  LED1 = LED - 3mm [color="Red (633nm)" current=0.030 package="3 mm [THT]"]
  LED2 = LED - 3mm [color="Yellow (595nm)" current=30mA package="3 mm [THT]"]
  LED3 = LED - 3mm [color="Green (555nm)" current=0.030 package="3 mm [THT]"]
  SM1 = 28BYJ-48 Stepper Motor [part_number=28BYJ-48]
  Driver1 = 28BYJ-48 Driver Module [part_number=ULN2003 package=THT]
  Mod1 = KY-022 Infrared Receiver Module [package="Breakout board"]
  R1 = Resistor [tolerance=±5% resistance=220 package="1206 [SMD]"]
  R2 = Resistor [tolerance=±5% resistance=220 package="1206 [SMD]"]
  R3 = Resistor [tolerance=±5% resistance=220 package="1206 [SMD]"]

nets:
  N1: Part1.D8, Mod1.S
  N2: Part1.D10_PWM/SS, Driver1.IN4
  N3: Part1.D11_PWM/MOSI, Driver1.IN3
  N4: Part1.D12/MISO, Driver1.IN2
  N5: Part1.D13/SCK, Driver1.IN1
  N6: Part1.D2, LED1.cathode
  N7: Part1.D3_PWM, LED3.cathode
  N8: Part1.D4, LED2.cathode
  5V: Part1.5V, Driver1.Vmotor, Mod1.Vin
  GND: Part1.GND, Driver1.GND, Mod1.-, R1.Pin_1, R2.Pin_1, R3.Pin_1
  N9: LED1.anode, R1.Pin_0
  N10: LED2.anode, R3.Pin_0
  N11: LED3.anode, R2.Pin_0
  N12: SM1.blue-pin, Driver1.blue-pin
  N13: SM1.pink-pin, Driver1.pink-pin
  N14: SM1.yellow-pin, Driver1.yellow-pin
  N15: SM1.orange-pin, Driver1.orange-pin
  N16: SM1.red-pin, Driver1.red-pin

custom parts:
  28BYJ-48 Stepper Motor: Unipolar Stepper Motor 28BYJ-48 Top coil - pink & orange Bottom coil - blue & yellow Common rail - red Connector pins: blue - pink - yellow - orange - red
  28BYJ-48 Driver Module: ULN2003 Driver Module for the 28BYJ-48 Unipolar Stepper Motor LED A - Blue wire - Bottom coil left LED B - Pink wire - Top coil left LED C - Yellow wire - Bottom coil right LED D - Orange wire - Top coil right Common rail - red Connector pins: blue - pink - yellow - orange - red Control pins - IN1 to IN4 Power pins - GND & Vmotor (5-12V) On/Off jumper (if removed, power to motor is cut).
  KY-022 Infrared Receiver Module: KY-022 IR receiver module, reacts to 38kHz infrared light.
