# Fritzing sketch schema1 (saved by Fritzing 0.9.10b)
breadboards: 2

parts:
  Part1 = HX711 Weighing Sensor Module
  Load_Cell1 = Load Cell - Red/white/black/green
  Part2 = Arduino Uno (Rev3)
  <20% = smd LED [color="Red (633nm)" package="1206 [SMD]"]
  >20% = smd LED [color="Green (555nm)" package="1206 [SMD]"]
  Ready? = smd LED [color="Blue (430nm)" package="1206 [SMD]"]
  S2 = Pushbutton [package="[THT]"]
  S3 = Pushbutton [package="[THT]"]
  S4 = Pushbutton [package="[THT]"]
  R1 = Resistor [tolerance=±5% resistance=10k package="2512 [SMD]"]
  R2 = Resistor [tolerance=±5% resistance=10k package="2512 [SMD]"]
  R3 = Resistor [tolerance=±5% resistance=10k package="2512 [SMD]"]
  Get_Ready = Pushbutton [package="[THT]"]
  R4 = Resistor [tolerance=±5% resistance=220 package="2512 [SMD]"]
  R5 = Resistor [tolerance=±5% resistance=220 package="2512 [SMD]"]
  R6 = Resistor [tolerance=±5% resistance=220 package="2512 [SMD]"]
  R7 = Resistor [tolerance=±5% resistance=10k package="2512 [SMD]"]
  J1 = Basic Servo
  SM1 = 28BYJ-48 Stepper Motor [part_number=28BYJ-48]
  Driver1 = 28BYJ-48 Driver Module [part_number=ULN2003 package=THT]

nets:
  VCC: Part1.VCC, Part2.5V, S2.Pin_1, S2.Pin_2, S3.Pin_1, S3.Pin_2, S4.Pin_1, S4.Pin_2, R4.Pin_1, J1.vcc, Driver1.Vmotor
  GND: Part1.GND, Part2.GND, <20%.cathode, >20%.cathode, Ready?.cathode, R1.Pin_0, R2.Pin_0, R3.Pin_0, Get_Ready.Pin_3, Get_Ready.Pin_4, R5.Pin_1, R6.Pin_1, R7.Pin_1, J1.gnd, Driver1.GND
  N1: Part1.DO/RX, Part2.D2
  N2: Part1.CK/TX, Part2.D3_PWM
  N3: Part1.E+, Load_Cell1.wire1
  N4: Part1.E-, Load_Cell1.wire3
  N5: Part1.A+, Load_Cell1.wire2
  N6: Part1.A-, Load_Cell1.wire4
  N7: Part2.D8, Get_Ready.Pin_1, Get_Ready.Pin_2, R7.Pin_0
  N8: Part2.D10_PWM/SS, J1.pulse
  N9: Part2.D11_PWM/MOSI, S3.Pin_3, S3.Pin_4, R1.Pin_1
  N10: Part2.D12/MISO, S4.Pin_3, S4.Pin_4, R2.Pin_1
  N11: Part2.D13/SCK, S2.Pin_3, S2.Pin_4, R3.Pin_1
  N12: Part2.D4, Driver1.IN4
  N13: Part2.D5_PWM, Driver1.IN3
  N14: Part2.D6_PWM, Driver1.IN2
  N15: Part2.D7, Driver1.IN1
  N16: <20%.anode, R5.Pin_0
  N17: >20%.anode, R4.Pin_0
  N18: Ready?.anode, R6.Pin_0
  N19: SM1.blue-pin, Driver1.blue-pin
  N20: SM1.pink-pin, Driver1.pink-pin
  N21: SM1.yellow-pin, Driver1.yellow-pin
  N22: SM1.orange-pin, Driver1.orange-pin
  N23: SM1.red-pin, Driver1.red-pin

custom parts:
  Load Cell - Red/white/black/green: A rectangle load cell/weighting pressure Sensor with four wires - Red, white, black, green. Normally corresponding with E+, E-, A+, A- respectively.
  28BYJ-48 Stepper Motor: Unipolar Stepper Motor 28BYJ-48 Top coil - pink & orange Bottom coil - blue & yellow Common rail - red Connector pins: blue - pink - yellow - orange - red
  28BYJ-48 Driver Module: ULN2003 Driver Module for the 28BYJ-48 Unipolar Stepper Motor LED A - Blue wire - Bottom coil left LED B - Pink wire - Top coil left LED C - Yellow wire - Bottom coil right LED D - Orange wire - Top coil right Common rail - red Connector pins: blue - pink - yellow - orange - red Control pins - IN1 to IN4 Power pins - GND & Vmotor (5-12V) On/Off jumper (if removed, power to motor is cut).
